// Digital circuit GPU.dig as structural Verilog
module GPU (
  input  CC,
  input  C,
  input  [31:0] Din,
  input  WE,
  input  [23:0] A,
  input  en,
  output [31:0] D,
  output [15:0] col,
  output Rect
);

  wire and_1_out, exe, onecolor, plotLine, plotLine_en, plotRect, pos;
  wire [0:0] Q_en;
  wire [8:0] dx, dy;
  wire [15:0] driver_1_out, plotline_1_addr, plotrect_1_addr;
  wire [31:0] Q_pos;
  wire [31:16] Q_onecolor;

  Demultiplexer #(.Selector_Bits(3)) demultiplexer_1 (
    .sel(Din[2:0]), .in(exe), .out_0(plotLine), .out_1(plotRect));  // open: out_2, out_3, out_4, out_5, out_6, out_7
  Register #(.Bits(32)) register_1 (.D(Din), .C(C), .en(pos), .Q(Q_pos));
  Register #(.Bits(32)) register_2 (.D(Din), .C(C), .en(onecolor), .Q({Q_onecolor, col}));
  and and_1 (and_1_out, WE, en);
  plotLine plotline_1 (
    .set(plotLine), .dx(dx), .dy(dy), .x_0(Q_pos[31:24]), .y_0(Q_pos[23:16]), .CC(CC),
    .addr(plotline_1_addr), .en(plotLine_en));
  plotRect plotrect_1 (
    .set(plotRect), .dx(dx), .dy(dy), .x_0(Q_pos[31:24]), .y_0(Q_pos[23:16]), .x_1(Q_pos[15:8]), .CC(CC),
    .addr(plotrect_1_addr), .en(Rect));
  Demultiplexer #(.Selector_Bits(3)) demultiplexer_2 (
    .sel(A[2:0]), .in(and_1_out), .out_0(exe), .out_2(pos), .out_3(onecolor));  // open: out_1, out_4, out_5, out_6, out_7
  Sub #(.Bits(9)) sub_1 (.a({1'b0, Q_pos[15:8]}), .b({1'b0, Q_pos[31:24]}), .c_i(1'b0), .s(dx));  // open: c_o
  assign driver_1_out = plotLine_en ? plotline_1_addr : 16'bz;  // Driver driver_1
  assign driver_1_out = Rect ? plotrect_1_addr : 16'bz;  // Driver driver_2
  Sub #(.Bits(9)) sub_2 (.a({1'b0, Q_pos[7:0]}), .b({1'b0, Q_pos[23:16]}), .c_i(1'b0), .s(dy));  // open: c_o
  GraphicCard #(.graphicHeight(256), .graphicWidth(256), .Bits(16)) graphiccard_1 (
    .A({1'b0, driver_1_out}), .str(Q_en[0]), .C(CC), .ld(1'b0), .B(1'b0), .D(col));
  Multiplexer #(.Selector_Bits(3), .Bits(32)) multiplexer_1 (
    .sel(A[2:0]), .in_0({{29{1'b0}}, Din[2:0]}), .in_1({{31{1'b0}}, Q_en[0]}), .in_2(Q_pos),
    .in_3({Q_onecolor, col}), .in_4({32{1'b0}}), .in_5({32{1'b0}}), .in_6({32{1'b0}}), .in_7({32{1'b0}}),
    .out(D));
  or or_1 (Q_en[0], plotLine_en, Rect);

  // Other names for the same wires on the sheet: Q_exe[2:0] = Din[2:0]; plotRect_en = Rect; Q_onecolor[15:0] = col;
  //   y_1[7:0] = Q_pos[7:0]; x_1[7:0] = Q_pos[15:8]; y_0[7:0] = Q_pos[23:16]; x_0[7:0] = Q_pos[31:24]; str = Q_en[0]

  // Notes on the sheet:
  //   CC: Hz: 5000
  //   C: Hz: 2
endmodule
