// Digital circuit top.dig as structural Verilog
module top (
);

  wire C, MemWrite, undriven, undriven_2, undriven_3;
  wire [2:0] undriven_4;
  wire [31:0] alu_1_result, ALUOut_q, Data_q, eepromdualport_1_d, extender_1_extended, IR_q,
       multiplexer_1_out, multiplexer_2_out, multiplexer_3_out, multiplexer_4_out, reg_file_1_rs1,
       reg_file_1_rs2, register_1_q, s1_q, s2_q, undriven_5, undriven_6;

  BlockRAMDualPort blockramdualport_1 ();  // open: A, Din, str, C, D
  Register register_1 (.D(undriven), .C(C), .en(undriven_2), .Q(register_1_q[0]));
  Multiplexer #(.Bits(32)) multiplexer_1 (
    .in_0(register_1_q), .in_1(multiplexer_4_out), .out(multiplexer_1_out));  // open: sel
  EEPROMDualPort #(.AddrBits(24), .Bits(32)) eepromdualport_1 (
    .A(multiplexer_1_out[23:0]), .Din(s2_q), .str(MemWrite), .C(C), .ld(1'b1), .D(eepromdualport_1_d));
  RegisterFile registerfile_1 ();  // open: Din, we, Rw, C, Ra, Rb, Da, Db
  Register #(.Bits(32)) IR (.D(eepromdualport_1_d), .C(C), .en(undriven_3), .Q(IR_q));
  D_FF #(.Bits(32)) Data (.D(eepromdualport_1_d), .C(C), .Q(Data_q));  // open: nQ
  REG_FILE reg_file_1 (
    .A_rs1(IR_q[19:15]), .A_rd(IR_q[11:7]), .WD(multiplexer_4_out), .C(C), .rs1(reg_file_1_rs1),
    .rs2(reg_file_1_rs2));  // open: WE, A_rs2
  Extender extender_1 (.src(undriven_4), .Imm(IR_q[31:7]), .Extended(extender_1_extended));
  D_FF #(.Bits(32)) s1 (.D(reg_file_1_rs1), .C(C), .Q(s1_q));  // open: nQ
  D_FF #(.Bits(32)) s2 (.D(reg_file_1_rs2), .C(C), .Q(s2_q));  // open: nQ
  Multiplexer #(.Bits(32), .Selector_Bits(2)) multiplexer_2 (
    .in_0(undriven_5), .in_1(undriven_6), .in_2(s1_q), .out(multiplexer_2_out));  // open: sel, in_3
  Multiplexer #(.Selector_Bits(2), .Bits(32)) multiplexer_3 (
    .in_0(s2_q), .in_1(extender_1_extended), .in_2(32'h1), .out(multiplexer_3_out));  // open: sel, in_3
  ALU alu_1 (.s1(multiplexer_2_out), .s2(multiplexer_3_out), .result(alu_1_result));  // open: Ctrl, zero
  D_FF #(.Bits(32)) ALUOut (.D(alu_1_result), .C(C), .Q(ALUOut_q));  // open: nQ
  Multiplexer #(.Bits(32), .Selector_Bits(2)) multiplexer_4 (
    .in_0(ALUOut_q), .in_1(Data_q), .in_2(alu_1_result), .out(multiplexer_4_out));  // open: sel, in_3
  // Pins of 1 and 32 bits meet at register_1_q
endmodule
